# Fritzing sketch Theif_detection (saved by Fritzing 1.0.2b)
breadboards: 1

parts:
  M1 = DOIT Esp32 DevKit v1 (30 pins long, 11 pins width) [part_number=ESP32S-PIN30]
  DFRobot_DFPlayer_Mini1 = DFRobot DFPlayer Mini [part_number=DFR0299]
  S1 = Pushbutton [package="[THT]"]
  LED1 = RGB LED - (4 legs) [color="Red (633nm)" current=0.030A package="5 mm [THT]"]
  ZS-042_RTC1 = ZS-042 RTC Module
  HC-SR04_Sensor_1 = HC-SR04 Ultrasonic Distance Sensor
  IR1 = TSOP312.., 314.. [package=THT]
  A1 = Micro SD card reader
  R1 = Resistor [tolerance=±5% resistance=220 package="2010 [SMD]"]
  R2 = Resistor [tolerance=±5% resistance=220 package="2010 [SMD]"]
  R3 = Resistor [tolerance=±5% resistance=220 package="2010 [SMD]"]
  SP1 = SPEAKER [package=pcb_mount_speaker]

nets:
  3V3: M1.3V3, DFRobot_DFPlayer_Mini1.VCC, A1.Pin_6
  GND: M1.GND, DFRobot_DFPlayer_Mini1.GND-1, DFRobot_DFPlayer_Mini1.GND-2, S1.Pin_1, S1.Pin_2, ZS-042_RTC1.GND, HC-SR04_Sensor_1.GND, IR1.GND, A1.Pin_1
  N1: M1.D4, R3.Pin_1
  N2: M1.RX2, DFRobot_DFPlayer_Mini1.RX
  N3: M1.TX2, DFRobot_DFPlayer_Mini1.TX
  N4: M1.D5, A1.Pin_5
  N5: M1.D18, A1.Pin_3
  N6: M1.D19, A1.Pin_2
  N7: M1.D21, ZS-042_RTC1.SDA
  N8: M1.D22, ZS-042_RTC1.SCL
  N9: M1.D23, A1.Pin_4
  N10: M1.D32, R1.Pin_1
  N11: M1.D33, R2.Pin_1
  N12: M1.D25, HC-SR04_Sensor_1.TRIG
  N13: M1.D26, HC-SR04_Sensor_1.ECHO
  N14: M1.D27, IR1.Data
  N15: M1.D13, S1.Pin_3, S1.Pin_4
  VCC: M1.VIN, ZS-042_RTC1.VCC, HC-SR04_Sensor_1.VCC, IR1.Vs
  N16: DFRobot_DFPlayer_Mini1.SPK_1, SP1.-
  N17: DFRobot_DFPlayer_Mini1.SPK_2, SP1.+
  N18: LED1.red_cathode, R1.Pin_0
  N19: LED1.green_cathode, R2.Pin_0
  N20: LED1.blue_cathode, R3.Pin_0

custom parts:
  DOIT Esp32 DevKit v1 (30 pins long, 11 pins width): The DOIT Esp32 DevKit v1 is one of the development board created by DOIT to evaluate the ESP-WROOM-32 module. It is based on the ESP32 microcontroller that boasts Wifi, Bluetooth, Ethernet and Low Power support all in a single chip. (vanepp) made breadboard work, adjusted pin numbering and labels and reduced size of schematic and cleaned up pcb. This chip is 30pins long (2 x15) and 11 pins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
  Micro SD card reader: Micro SD card reader.
